# Fritzing sketch sonar (saved by Fritzing 0.9.3b)
breadboards: 1

parts:
  Micro_bit1 = Microbit
  hc-sr1 = hc-sr04

nets:
  GND: Micro_bit1.GND, hc-sr1.GND
  N1: Micro_bit1.3V, hc-sr1.VCC
  N2: Micro_bit1.1, hc-sr1.Trig
  N3: Micro_bit1.2, hc-sr1.Echo

custom parts:
  Microbit: BBC Microbit Fritzing part
